# Fritzing sketch 1Segment (saved by Fritzing 0.9.2b)
circuit board: 6.88566cm x 5.36311cm
breadboards: 1

parts:
  Digit_4 = 7 Segment Display
  PCB1 = Arduino Shield PCB  # not connected
  part = female pin header, 1 pin [form="♀ (female)"]  # not connected
  Arduino1 = Arduino Uno (Rev3)

nets:
  N1: Digit_4.Segment_E, Arduino1.D6_PWM
  N2: Digit_4.Segment_D, Arduino1.D5_PWM
  N3: Digit_4.common_anode, Arduino1.D13/SCK
  N4: Digit_4.Segment_C, Arduino1.D11_PWM/MOSI
  N5: Digit_4.Segment_DP, Arduino1.D4
  N6: Digit_4.Segment_B, Arduino1.D3_PWM
  N7: Digit_4.Segment_A, Arduino1.D2
  N8: Digit_4.Segment_F, Arduino1.D7
  N9: Digit_4.Segment_G, Arduino1.D12/MISO

custom parts:
  Arduino Shield PCB: Plain PCB Shaped to fit an Arduino "Shield"

// code stored in the sketch: 7Segment_direct.ino

